# Fritzing sketch schematic (saved by Fritzing 0.9.10b)
perfboards: 1

parts:
  R3 = Resistor [tolerance=±5% power=0.25 resistance=22k package=THT]
  R4 = Trimmer Potentiometer [maximum_resistance=10kΩ knob_status=50% power=0.5W package=THT]
  R5 = Resistor [tolerance=±5% power=0.25 resistance=22k package=THT]
  R6 = Resistor [tolerance=±5% power=0.25 resistance=470k package=THT]
  LM1 = LM741 [part_number=LM741 package="DIP (Dual Inline) [THT]"]
  R7 = Resistor [tolerance=±5% power=0.25 resistance=10 package=THT]
  R8 = Resistor [tolerance=±5% power=0.25 resistance=1k package=THT]
  LED1 = smd LED [color="Green (560nm)" package="0603 [SMD]"]
  R9 = Resistor [tolerance=±5% power=0.25 resistance=1k package=THT]
  J1 = top view banana jack black [package=THT]
  J2 = top view banana jack black [package=THT]
  VCC2 = Battery block 9V
  J3 = Piezo Speaker
  R10 = Resistor [tolerance=±5% power=0.25 resistance=1k package=THT]
  LED2 = smd LED [color="Red (633nm)" package="0603 [SMD]"]
  R11 = Resistor [tolerance=±5% power=0.25 resistance=1k package=THT]
  S4 = Pushbutton [package=THT]

nets (from the schematic view):
  N1: R3.Pin_0, R6.Pin_0, LM1.pin7, LED1.anode, VCC2.+, J3.pin2, R11.Pin_0
  N2: R3.Pin_1, R7.Pin_0, R9.Pin_1, J1.pin1
  N3: R4.leg1, LM1.pin3, R9.Pin_0
  N4: R4.wiper, R6.Pin_1
  N5: R4.leg2, LM1.pin2, R8.Pin_0
  N6: R5.Pin_0, R7.Pin_1, R8.Pin_1, J2.pin1
  N7: R5.Pin_1, LM1.pin4, LED2.cathode, S4.leg0
  N8: LM1.pin6, J3.pin1, R10.Pin_1
  N9: LED1.cathode, R10.Pin_0
  N10: VCC2.-, S4.leg1
  N11: LED2.anode, R11.Pin_1

custom parts:
  LM741: This is a single Op Amp DIP.
  top view banana jack black: Top view banana jack black.
